// Logisim project Simulador_Relogio.circ as structural Verilog: 8 circuits, main circuit Simulador Relógio
module \Relogio_padrão  (
  input  CLK,
  input  Pause,
  input  RESET,
  input  Select,
  input  Mode,
  input  ALTER,
  output [3:0] DHA,
  output [3:0] UHA,
  output [3:0] DMA,
  output [3:0] UMA,
  output [3:0] DSA,
  output [3:0] USA
);

  wire _0_59_2_next, _0_59_next, and_4_out, and_5_out, and_6_out, and_7_out, and_8_out, and_9_out, C, H, Hrs,
       M, Min, N, not_1_out, not_2_out, not_3_out, or_1_out, or_2_out, or_3_out, or_4_out, S, Seg;

  and and_1 (H, C, Hrs, ALTER);
  and and_2 (M, C, Min, ALTER);
  and and_3 (S, C, Seg, ALTER);
  _0_23 _0_23 (.DEZENA(DHA), .UNIDADE(UHA), .CLK(or_1_out), .RESET(and_6_out), .Pause(Pause));  // open: NEXT
  or or_1 (or_1_out, and_4_out, and_5_out);
  and and_4 (and_4_out, _0_59_next, not_1_out);
  and and_5 (and_5_out, H, C);
  not not_1 (not_1_out, C);
  and and_6 (and_6_out, RESET, or_2_out);
  or or_2 (or_2_out, C, N);
  _0_59 _0_59 (.DEZENA(DMA), .NEXT(_0_59_next), .UNIDADE(UMA), .CLK(or_3_out), .RESET(and_6_out), .Pause(Pause));
  or or_3 (or_3_out, and_7_out, and_8_out);
  and and_7 (and_7_out, _0_59_2_next, not_2_out);
  and and_8 (and_8_out, M, C);
  not not_2 (not_2_out, C);
  \Opção  \Opção  (.Select(Select), .Z(Hrs), .Y(Min), .X(Seg));
  _0_59 _0_59_2 (.DEZENA(DSA), .NEXT(_0_59_2_next), .UNIDADE(USA), .CLK(or_4_out), .RESET(and_6_out), .Pause(Pause));
  or or_4 (or_4_out, and_9_out, S);
  and and_9 (and_9_out, CLK, not_3_out);
  not not_3 (not_3_out, C);
  \Opção  \Opção_2  (.Select(Mode), .Z(C), .X(N));  // open: Y

  // Other names for the same wires on the sheet: ALT = ALTER
endmodule

module _0_9 (
  input  Pause,
  input  CLK,
  input  RST,
  output [3:0] out_4,
  output out_5
);

  wire not_1_out, not_2_out, not_3_out, or_1_out;
  wire [3:0] adder_1_out;

  not not_1 (not_1_out, Pause);
  Hex_Digit_Display hex_digit_display_1 (.value(out_4));  // open: dp
  Register #(.width(4)) Registrador (.D(adder_1_out), .en(not_1_out), .Q(out_4), .clk(CLK), .clr(or_1_out));
  or or_1 (or_1_out, out_5, RST);
  not not_2 (not_2_out, out_4[2]);
  not not_3 (not_3_out, out_4[0]);
  and and_1 (out_5, out_4[3], not_2_out, out_4[1], not_3_out);
  Adder #(.width(4)) adder_1 (.a(out_4), .b(4'b0001), .out(adder_1_out));  // open: cin, cout

  // Notes on the sheet:
  //   Somador
endmodule

module _0_59 (
  input  CLK,
  input  RESET,
  input  Pause,
  output [3:0] DEZENA,
  output [3:0] UNIDADE,
  output NEXT
);

  wire _0_9_2_out_5, not_1_out, not_2_out, or_1_out;

  not not_1 (not_1_out, DEZENA[0]);
  and and_1 (NEXT, not_1_out, DEZENA[1], DEZENA[2], not_2_out);
  not not_2 (not_2_out, DEZENA[3]);
  Hex_Digit_Display hex_digit_display_1 (.value(DEZENA));  // open: dp
  _0_9 _0_9 (.CLK(_0_9_2_out_5), .out_4(DEZENA), .RST(or_1_out));  // open: out_5, Pause
  or or_1 (or_1_out, NEXT, RESET);
  Hex_Digit_Display hex_digit_display_2 (.value(UNIDADE));  // open: dp
  _0_9 _0_9_2 (.CLK(CLK), .out_5(_0_9_2_out_5), .out_4(UNIDADE), .RST(or_1_out), .Pause(Pause));
endmodule

module _0_23 (
  input  CLK,
  input  Pause,
  input  RESET,
  output [3:0] DEZENA,
  output [3:0] UNIDADE,
  output NEXT
);

  wire _0_9_2_out_5, not_1_out, not_2_out, not_3_out, not_4_out, not_5_out, not_6_out, or_1_out;

  not not_1 (not_1_out, DEZENA[0]);
  not not_2 (not_2_out, DEZENA[2]);
  not not_3 (not_3_out, DEZENA[3]);
  and and_1 (NEXT, not_1_out, DEZENA[1], not_2_out, not_3_out, not_4_out, not_5_out, UNIDADE[2], not_6_out);
  not not_4 (not_4_out, UNIDADE[0]);
  not not_5 (not_5_out, UNIDADE[1]);
  not not_6 (not_6_out, UNIDADE[3]);
  Hex_Digit_Display hex_digit_display_1 (.value(DEZENA));  // open: dp
  _0_9 _0_9 (.CLK(_0_9_2_out_5), .out_4(DEZENA), .RST(or_1_out));  // open: out_5, Pause
  or or_1 (or_1_out, NEXT, RESET);
  _0_9 _0_9_2 (.CLK(CLK), .out_5(_0_9_2_out_5), .out_4(UNIDADE), .RST(or_1_out), .Pause(Pause));
  Hex_Digit_Display hex_digit_display_2 (.value(UNIDADE));  // open: dp
endmodule

module \Simulador_Relógio  (
  input  in_1
);

  wire A, ALARME, ALTER, C, clock_1_out, H, M, MODE, MUD, N, \Opção_2_x , \Opção_2_y , \Opção_2_z , RST, S,
       SELECT;
  wire [3:0] DH, DHA, DHR, DM, DMA, DMR, DS, DSA, DSR, UH, UHA, UHR, UM, UMA, UMR, US, USA, USR;

  Clock clock_1 (.out(clock_1_out));
  \Relogio_padrão  \relogio_padrão_1  (
    .CLK(clock_1_out), .DHA(DHR), .UHA(UHR), .DMA(DMR), .UMA(UMR), .DSA(DSR), .USA(USR), .RESET(RST),
    .Pause(in_1), .ALTER(ALTER), .Mode(MODE), .Select(SELECT));
  Button button_1 (.out(SELECT));
  LED led_1 (.in(H));
  Hex_Digit_Display hex_digit_display_1 (.value(UH));  // open: dp
  Hex_Digit_Display hex_digit_display_2 (.value(DH));  // open: dp
  LED led_2 (.in(C));
  LED led_3 (.in(M));
  Hex_Digit_Display hex_digit_display_3 (.value(DM));  // open: dp
  LED led_4 (.in(A));
  Alarme alarme_1 (
    .A(A), .Alter(ALTER), .DHA(DHA), .UHA(UHA), .DMA(DMA), .UMA(UMA), .DSA(DSA), .USA(USA), .RESET(RST),
    .Select(SELECT));
  or or_1 (MUD, C, A);
  Hex_Digit_Display hex_digit_display_4 (.value(UM));  // open: dp
  LED led_5 (.in(ALARME));
  LED led_6 (.in(S));
  Hex_Digit_Display hex_digit_display_5 (.value(DS));  // open: dp
  Hex_Digit_Display hex_digit_display_6 (.value(US));  // open: dp
  LED led_7 (.in(N));
  \Opção  \Opção  (.Select(MODE), .Z(C), .Y(A), .X(N));
  and and_1 (H, MUD, \Opção_2_z );
  \Opção  \Opção_2  (.Select(SELECT), .Z(\Opção_2_z ), .Y(\Opção_2_y ), .X(\Opção_2_x ));
  Button button_2 (.out(MODE));
  Button button_3 (.out(ALTER));
  and and_2 (M, \Opção_2_y , MUD);
  and and_3 (S, MUD, \Opção_2_x );
  Button button_4 (.out(RST));
  D_E d_e_1 (
    .USR(USR), .USA(USA), .DSR(DSR), .DSA(DSA), .UMR(UMR), .UMA(UMA), .DMR(DMR), .DMA(DMA), .UHR(UHR),
    .UHA(UHA), .DHR(DHR), .DHA(DHA), .Alarme(ALARME), .A(A), .US(US), .DS(DS), .UM(UM), .DM(DM), .UH(UH),
    .DH(DH));

  // Other names for the same wires on the sheet: PAUSE = in_1
endmodule

module \Opção  (
  input  Select,
  output Z,
  output Y,
  output X
);

  wire and_4_out, not_1_out, not_2_out, not_3_out, not_4_out;
  wire [1:0] Contador_q;

  not not_1 (not_1_out, Contador_q[0]);
  and and_1 (Z, not_1_out, Contador_q[1]);
  and and_2 (Y, Contador_q[0], not_2_out);
  not not_2 (not_2_out, Contador_q[1]);
  not not_3 (not_3_out, Contador_q[0]);
  and and_3 (X, not_3_out, not_4_out);
  not not_4 (not_4_out, Contador_q[1]);
  Counter #(.width(2), .max('h3)) Contador (
    .Q(Contador_q), .clk(Select), .clr(and_4_out));  // open: load, D, count, carry
  and and_4 (and_4_out, Contador_q[0], Contador_q[1]);
endmodule

// Des. e Exi.
module D_E (
  input  [3:0] USR,
  input  [3:0] USA,
  input  A,
  input  [3:0] DSR,
  input  [3:0] DSA,
  input  [3:0] UMR,
  input  [3:0] UMA,
  input  [3:0] DMR,
  input  [3:0] DMA,
  input  [3:0] UHR,
  input  [3:0] UHA,
  input  [3:0] DHR,
  input  [3:0] DHA,
  output [3:0] US,
  output [3:0] DS,
  output Alarme,
  output [3:0] UM,
  output [3:0] DM,
  output [3:0] UH,
  output [3:0] DH
);

  wire and_1_out, and_2_out, and_3_out, and_4_out, and_5_out, comparator_1_eq, comparator_1_gt,
       comparator_2_eq, comparator_2_gt, comparator_3_eq, comparator_3_gt, comparator_4_eq, comparator_4_gt,
       comparator_5_eq, comparator_5_gt, comparator_6_eq, comparator_6_gt, or_1_out;

  Comparator #(.width(4)) comparator_1 (.a(USR), .b(USA), .gt(comparator_1_gt), .eq(comparator_1_eq));  // open: lt
  Comparator #(.width(4)) comparator_2 (.a(DSR), .b(DSA), .gt(comparator_2_gt), .eq(comparator_2_eq));  // open: lt
  Comparator #(.width(4)) comparator_3 (.a(UMR), .b(UMA), .gt(comparator_3_gt), .eq(comparator_3_eq));  // open: lt
  Comparator #(.width(4)) comparator_4 (.a(DMR), .b(DMA), .gt(comparator_4_gt), .eq(comparator_4_eq));  // open: lt
  Comparator #(.width(4)) comparator_5 (.a(UHR), .b(UHA), .gt(comparator_5_gt), .eq(comparator_5_eq));  // open: lt
  Comparator #(.width(4)) comparator_6 (.a(DHR), .b(DHA), .gt(comparator_6_gt), .eq(comparator_6_eq));  // open: lt
  or or_1 (or_1_out, comparator_1_gt, comparator_1_eq);
  and and_1 (and_1_out, or_1_out, comparator_2_eq, comparator_3_eq, comparator_4_eq, comparator_5_eq, comparator_6_eq);
  and and_2 (and_2_out, comparator_2_gt, comparator_3_eq, comparator_4_eq, comparator_5_eq, comparator_6_eq);
  and and_3 (and_3_out, comparator_3_gt, comparator_4_eq, comparator_5_eq, comparator_6_eq);
  and and_4 (and_4_out, comparator_4_gt, comparator_5_eq, comparator_6_eq);
  and and_5 (and_5_out, comparator_5_gt, comparator_6_eq);
  or or_2 (Alarme, and_1_out, and_2_out, and_3_out, and_4_out, and_5_out, comparator_6_gt);
  Multiplexer #(.width(4), .enable("false")) multiplexer_1 (.in0(USR), .in1(USA), .out(US), .sel(A));
  Multiplexer #(.width(4), .enable("false")) multiplexer_2 (.in0(DSR), .in1(DSA), .out(DS), .sel(A));
  Multiplexer #(.width(4), .enable("false")) multiplexer_3 (.in0(UMR), .in1(UMA), .out(UM), .sel(A));
  Multiplexer #(.width(4), .enable("false")) multiplexer_4 (.in0(DMR), .in1(DMA), .out(DM), .sel(A));
  Multiplexer #(.width(4), .enable("false")) multiplexer_5 (.in0(UHR), .in1(UHA), .out(UH), .sel(A));
  Multiplexer #(.width(4), .enable("false")) multiplexer_6 (.in0(DHR), .in1(DHA), .out(DH), .sel(A));
endmodule

module Alarme (
  input  A,
  input  Select,
  input  Alter,
  input  RESET,
  output [3:0] DHA,
  output [3:0] UHA,
  output [3:0] DMA,
  output [3:0] UMA,
  output [3:0] DSA,
  output [3:0] USA
);

  wire and_4_out, H, Hrs, M, Min, S, Seg;

  and and_1 (H, A, Hrs, Alter);
  \Opção  \Opção  (.Select(Select), .Z(Hrs), .Y(Min), .X(Seg));
  and and_2 (M, A, Min, Alter);
  _0_23 _0_23 (.DEZENA(DHA), .UNIDADE(UHA), .CLK(H), .RESET(and_4_out));  // open: NEXT, Pause
  and and_3 (S, A, Seg, Alter);
  and and_4 (and_4_out, RESET, A);
  _0_59 _0_9 (.DEZENA(DMA), .UNIDADE(UMA), .CLK(M), .RESET(and_4_out));  // open: NEXT, Pause
  _0_59 _0_9_2 (.DEZENA(DSA), .UNIDADE(USA), .CLK(S), .RESET(and_4_out));  // open: NEXT, Pause

  // Other names for the same wires on the sheet: ALT = Alter
endmodule
